# Fritzing sketch axoloti_tremolo_fx-hardware_layout (saved by Fritzing 0.9.0b)
breadboards: 1

parts:
  R2 = Rotary Potentiometer (Small) [maximum_resistance=100kΩ package=THT]
  R3 = Rotary Potentiometer (Small) [maximum_resistance=100kΩ package=THT]
  R4 = Rotary Potentiometer (Small) [maximum_resistance=100kΩ package=THT]
  R5 = Rotary Potentiometer (Small) [maximum_resistance=100kΩ package=THT]
  LED1 = LED - 5mm [color="Red (633nm)" package="5 mm [THT]"]
  R6 = Resistor [tolerance=±5% resistance=220 package=THT]

nets:
  N1: R2.leg1, R3.leg1, R4.leg1, R5.leg1
  N2: R2.leg2, R3.leg2, R4.leg2, R5.leg2
  N3: LED1.anode, R6.Pin_0

notes:
  AXOLOTI CORE
  Axoloti Tremolo FX Layout.
  Potentiometers are 10k
  LED resistor is 220 Ohm
